# Fritzing sketch Prototype (saved by Fritzing 0.9.3b)
breadboards: 1

parts:
  Part1 = Arduino Uno (Rev3)
  RY1 = KF-301 Relay [package=THT]
  VALVE1 = Plastic Solenoid Valve
  R1 = Resistor [tolerance=±5% resistance=220 package="2010 [SMD]"]
  S1 = Pushbutton [package="[SMD]"]

nets:
  N1: Part1.D3_PWM, RY1.signal
  N2: Part1.D7, R1.Pin_0, S1.Pin_1, S1.Pin_2
  N3: Part1.5V, RY1.power, S1.Pin_3, S1.Pin_4
  N4: Part1.GND, RY1.ground, R1.Pin_1
  N5: RY1.NO, VALVE1.no_name_yet#1

custom parts:
  KF-301 Relay: KF-301 SPDT Relay module using SRD-05VDC-SL-C relay.
